// Logisim project ETFStudent.circ as structural Verilog: 11 circuits, main circuit REG32_LD
module REG32_LD (
  input  [31:0] I15__0,
  input  LD,
  input  mr,
  input  CLK,
  output [31:0] A15__0
);

  // REG16_LD reg16_ld_1: pin names not known; wires that end beside it: CLK, mr, I15__0[31:16], A15__0[31:16], LD
  // REG16_LD reg16_ld_2: pin names not known; wires that end beside it: CLK, mr, I15__0[15:0], A15__0[15:0], LD

  // Notes on the sheet:
  //   __
endmodule

module KMOPR (
  input  LD,
  input  ST,
  input  ADD,
  input  SUB,
  input  CMP,
  input  JADR,
  input  CLR,
  input  JMP,
  input  JSR,
  input  BLEQ,
  input  JEQ,
  input  JGRTU,
  input  JGRT,
  input  HALT,
  input  RTS,
  input  RTI,
  input  INC,
  input  PUSH,
  input  POP,
  output [5:0] Adr5__0
);

  assign Adr5__0 = LD ? 6'b000010 : 6'bz;  // Controlled_Buffer controlled_buffer_1
  assign Adr5__0 = ST ? 6'b000100 : 6'bz;  // Controlled_Buffer controlled_buffer_2
  assign Adr5__0 = ADD ? 6'b001010 : 6'bz;  // Controlled_Buffer controlled_buffer_3
  assign Adr5__0 = SUB ? 6'b001100 : 6'bz;  // Controlled_Buffer controlled_buffer_4
  assign Adr5__0 = CMP ? 6'b001110 : 6'bz;  // Controlled_Buffer controlled_buffer_5
  assign Adr5__0 = JADR ? 6'b001111 : 6'bz;  // Controlled_Buffer controlled_buffer_6
  assign Adr5__0 = CLR ? 6'b010001 : 6'bz;  // Controlled_Buffer controlled_buffer_7
  assign Adr5__0 = JMP ? 6'b010010 : 6'bz;  // Controlled_Buffer controlled_buffer_8
  assign Adr5__0 = JSR ? 6'b010011 : 6'bz;  // Controlled_Buffer controlled_buffer_9
  assign Adr5__0 = BLEQ ? 6'b010110 : 6'bz;  // Controlled_Buffer controlled_buffer_10
  assign Adr5__0 = JEQ ? 6'b011000 : 6'bz;  // Controlled_Buffer controlled_buffer_11
  assign Adr5__0 = JGRTU ? 6'b011000 : 6'bz;  // Controlled_Buffer controlled_buffer_12
  assign Adr5__0 = JGRT ? 6'b011000 : 6'bz;  // Controlled_Buffer controlled_buffer_13
  assign Adr5__0 = HALT ? 6'b011010 : 6'bz;  // Controlled_Buffer controlled_buffer_14
  assign Adr5__0 = RTS ? 6'b011011 : 6'bz;  // Controlled_Buffer controlled_buffer_15
  assign Adr5__0 = RTI ? 6'b011111 : 6'bz;  // Controlled_Buffer controlled_buffer_16
  assign Adr5__0 = INC ? 6'b100101 : 6'bz;  // Controlled_Buffer controlled_buffer_17
  assign Adr5__0 = PUSH ? 6'b100111 : 6'bz;  // Controlled_Buffer controlled_buffer_18
  assign Adr5__0 = POP ? 6'b101011 : 6'bz;  // Controlled_Buffer controlled_buffer_19
endmodule

module REG6_INC_LD (
  input  [5:0] I5__0,
  input  LD,
  input  INC,
  input  mr,
  input  CLK,
  output [5:0] A5__0
);

  wire reg2m_inc_ld_1_p7, reg2m_inc_ld_2_p8;

  // REG2m_INC_LD reg2m_inc_ld_1: pin names not known; wires that end beside it: CLK, mr, I5__0[5:4], A5__0[5:4], LD, INC, reg2m_inc_ld_1_p7
  // REG2m_INC_LD reg2m_inc_ld_2: pin names not known; wires that end beside it: CLK, reg2m_inc_ld_1_p7, mr, I5__0[3:2], A5__0[3:2], LD, INC, reg2m_inc_ld_2_p8
  // REG2m_INC_LD reg2m_inc_ld_3: pin names not known; wires that end beside it: CLK, reg2m_inc_ld_2_p8, mr, I5__0[1:0], A5__0[1:0], LD, INC, INC

  // Notes on the sheet:
  //   __
endmodule

module MEM64Kx16 (
  input  WR_RD,
  input  [15:0] A15__0,
  input  [15:0] DIN,
  input  CS,
  input  CLK,
  output [15:0] DOUT
);

  wire not_1_out;

  not not_1 (not_1_out, WR_RD);
  RAM #(.addrWidth(16), .dataWidth(16), .bus("separate")) ram_1 (
    .addr(A15__0), .din(DIN), .data(DOUT), .str(WR_RD), .sel(CS), .clk(CLK), .ld(not_1_out), .clr(1'b0));

  // Notes on the sheet:
  //   __
endmodule

module KMADR (
  input  immed,
  input  memdir,
  input  regdir,
  input  preincr,
  input  postdec,
  input  regindpom,
  output [4:0] A4__0
);

  assign A4__0 = immed ? 5'b00010 : 5'bz;  // Controlled_Buffer controlled_buffer_1
  assign A4__0 = memdir ? 5'b00011 : 5'bz;  // Controlled_Buffer controlled_buffer_2
  assign A4__0 = regdir ? 5'b00100 : 5'bz;  // Controlled_Buffer controlled_buffer_3
  assign A4__0 = preincr ? 5'b00110 : 5'bz;  // Controlled_Buffer controlled_buffer_4
  assign A4__0 = postdec ? 5'b01001 : 5'bz;  // Controlled_Buffer controlled_buffer_5
  assign A4__0 = regindpom ? 5'b01100 : 5'bz;  // Controlled_Buffer controlled_buffer_6
endmodule

module GPR32x16 (
  input  in_1,
  input  in_2,
  input  in_3,
  input  in_4,
  input  [15:0] DIN15__0,
  input  rst,
  input  WR,
  input  CLK,
  input  in_9,
  input  [4:0] A4__0,
  output [15:0] DOUT15__0
);

  wire and_3_out, and_4_out, CS0, CS1, CS2, CS3, CS4, CS5, CS6, CS7, CS8, CS9, CS10, CS11, CS12, CS13, CS14,
       CS15, CS16, CS17, CS18, CS19, CS20, CS21, CS22, CS23, CS24, CS25, CS26, CS27, CS28, CS29, CS30, CS31,
       dc1_2_1_p3, dc1_2_1_p4, mp2_16b_1_p3, not_1_out, reg16_1_p5, reg16_ld_1_p4, reg16_ld_2_p4,
       reg16_ld_3_p4, reg16_ld_4_p4, reg16_ld_5_p4, reg16_ld_6_p4, reg16_ld_7_p4, reg16_ld_8_p4,
       reg16_ld_9_p4, reg16_ld_10_p4, reg16_ld_11_p4, reg16_ld_12_p4, reg16_ld_13_p4, reg16_ld_14_p4,
       reg16_ld_15_p4, reg16_ld_16_p4, reg16_ld_17_p4, reg16_ld_18_p4, reg16_ld_19_p4, reg16_ld_20_p4,
       reg16_ld_21_p4, reg16_ld_22_p4, reg16_ld_23_p4, reg16_ld_24_p4, reg16_ld_25_p4, reg16_ld_26_p4,
       reg16_ld_27_p4, reg16_ld_28_p4, reg16_ld_29_p4, reg16_ld_30_p4, reg16m_inc_ld_1_p4;
  wire [15:0] reg16_1_p4, reg16_ld_1_p3, reg16_ld_2_p3, reg16_ld_3_p3, reg16_ld_4_p3, reg16_ld_5_p3,
       reg16_ld_6_p3, reg16_ld_7_p3, reg16_ld_8_p3, reg16_ld_9_p3, reg16_ld_10_p3, reg16_ld_11_p3,
       reg16_ld_12_p3, reg16_ld_13_p3, reg16_ld_14_p3, reg16_ld_15_p3, reg16_ld_16_p3, reg16_ld_17_p3,
       reg16_ld_18_p3, reg16_ld_19_p3, reg16_ld_20_p3, reg16_ld_21_p3, reg16_ld_22_p3, reg16_ld_23_p3,
       reg16_ld_24_p3, reg16_ld_25_p3, reg16_ld_26_p3, reg16_ld_27_p3, reg16_ld_28_p3, reg16_ld_29_p3,
       reg16_ld_30_p3, reg16m_inc_ld_1_p3;

  // DC1_2 dc1_2_1: pin names not known; wires that end beside it: A4__0[4], 1'b1, dc1_2_1_p3, dc1_2_1_p4
  // DC4_16 dc4_16_1: pin names not known; wires that end beside it: A4__0[3:0], dc1_2_1_p3, CS0, CS1, CS2, CS3, CS4, CS5, CS6, CS7, CS8, CS9, CS10, CS11, CS12, CS13, CS14, CS15
  // DC4_16 dc4_16_2: pin names not known; wires that end beside it: A4__0[3:0], dc1_2_1_p4, CS16, CS17, CS18, CS19, CS20, CS21, CS22, CS23, CS24, CS25, CS26, CS27, CS28, CS29, CS30, CS31
  not not_1 (not_1_out, rst);
  // REG16 reg16_1: pin names not known; wires that end beside it: CLK, not_1_out, DIN15__0, reg16_1_p4, reg16_1_p5, in_1, in_4
  assign DOUT15__0 = CS0 ? reg16_1_p4 : 16'bz;  // Controlled_Buffer controlled_buffer_1
  // MP2_16b mp2_16b_1: pin names not known; wires that end beside it: rst, DIN15__0, mp2_16b_1_p3, 16'h1000, 1'b1
  // REG16m_INC_LD reg16m_inc_ld_1: pin names not known; wires that end beside it: CLK, mp2_16b_1_p3, reg16m_inc_ld_1_p3, reg16m_inc_ld_1_p4, in_9, 1'b1
  assign DOUT15__0 = CS1 ? reg16m_inc_ld_1_p3 : 16'bz;  // Controlled_Buffer controlled_buffer_2
  // REG16_LD reg16_ld_1: pin names not known; wires that end beside it: CLK, DIN15__0, reg16_ld_1_p3, reg16_ld_1_p4
  assign DOUT15__0 = CS4 ? reg16_ld_1_p3 : 16'bz;  // Controlled_Buffer controlled_buffer_3
  // REG16_LD reg16_ld_2: pin names not known; wires that end beside it: CLK, DIN15__0, reg16_ld_2_p3, reg16_ld_2_p4
  assign DOUT15__0 = CS6 ? reg16_ld_2_p3 : 16'bz;  // Controlled_Buffer controlled_buffer_4
  and and_1 (reg16_ld_1_p4, CS4, WR);
  and and_2 (reg16_ld_2_p4, CS6, WR);
  and and_3 (and_3_out, CS0, WR);
  or or_1 (reg16_1_p5, and_3_out, in_3);
  or or_2 (reg16m_inc_ld_1_p4, and_4_out, in_2, rst);
  and and_4 (and_4_out, CS1, WR);
  // REG16_LD reg16_ld_3: pin names not known; wires that end beside it: CLK, DIN15__0, reg16_ld_3_p3, reg16_ld_3_p4
  assign DOUT15__0 = CS2 ? reg16_ld_3_p3 : 16'bz;  // Controlled_Buffer controlled_buffer_5
  // REG16_LD reg16_ld_4: pin names not known; wires that end beside it: CLK, DIN15__0, reg16_ld_4_p3, reg16_ld_4_p4
  assign DOUT15__0 = CS3 ? reg16_ld_4_p3 : 16'bz;  // Controlled_Buffer controlled_buffer_6
  // REG16_LD reg16_ld_5: pin names not known; wires that end beside it: CLK, DIN15__0, reg16_ld_5_p3, reg16_ld_5_p4
  assign DOUT15__0 = CS5 ? reg16_ld_5_p3 : 16'bz;  // Controlled_Buffer controlled_buffer_7
  // REG16_LD reg16_ld_6: pin names not known; wires that end beside it: CLK, DIN15__0, reg16_ld_6_p3, reg16_ld_6_p4
  assign DOUT15__0 = CS7 ? reg16_ld_6_p3 : 16'bz;  // Controlled_Buffer controlled_buffer_8
  and and_5 (reg16_ld_3_p4, CS2, WR);
  and and_6 (reg16_ld_4_p4, CS3, WR);
  and and_7 (reg16_ld_5_p4, CS5, WR);
  and and_8 (reg16_ld_6_p4, CS7, WR);
  // REG16_LD reg16_ld_7: pin names not known; wires that end beside it: CLK, DIN15__0, reg16_ld_7_p3, reg16_ld_7_p4
  assign DOUT15__0 = CS8 ? reg16_ld_7_p3 : 16'bz;  // Controlled_Buffer controlled_buffer_9
  // REG16_LD reg16_ld_8: pin names not known; wires that end beside it: CLK, DIN15__0, reg16_ld_8_p3, reg16_ld_8_p4
  assign DOUT15__0 = CS10 ? reg16_ld_8_p3 : 16'bz;  // Controlled_Buffer controlled_buffer_10
  // REG16_LD reg16_ld_9: pin names not known; wires that end beside it: CLK, DIN15__0, reg16_ld_9_p3, reg16_ld_9_p4
  assign DOUT15__0 = CS12 ? reg16_ld_9_p3 : 16'bz;  // Controlled_Buffer controlled_buffer_11
  // REG16_LD reg16_ld_10: pin names not known; wires that end beside it: CLK, DIN15__0, reg16_ld_10_p3, reg16_ld_10_p4
  assign DOUT15__0 = CS14 ? reg16_ld_10_p3 : 16'bz;  // Controlled_Buffer controlled_buffer_12
  and and_9 (reg16_ld_7_p4, CS8, WR);
  and and_10 (reg16_ld_8_p4, CS10, WR);
  and and_11 (reg16_ld_9_p4, CS12, WR);
  and and_12 (reg16_ld_10_p4, CS14, WR);
  // REG16_LD reg16_ld_11: pin names not known; wires that end beside it: CLK, DIN15__0, reg16_ld_11_p3, reg16_ld_11_p4
  assign DOUT15__0 = CS9 ? reg16_ld_11_p3 : 16'bz;  // Controlled_Buffer controlled_buffer_13
  // REG16_LD reg16_ld_12: pin names not known; wires that end beside it: CLK, DIN15__0, reg16_ld_12_p3, reg16_ld_12_p4
  assign DOUT15__0 = CS11 ? reg16_ld_12_p3 : 16'bz;  // Controlled_Buffer controlled_buffer_14
  // REG16_LD reg16_ld_13: pin names not known; wires that end beside it: CLK, DIN15__0, reg16_ld_13_p3, reg16_ld_13_p4
  assign DOUT15__0 = CS13 ? reg16_ld_13_p3 : 16'bz;  // Controlled_Buffer controlled_buffer_15
  // REG16_LD reg16_ld_14: pin names not known; wires that end beside it: CLK, DIN15__0, reg16_ld_14_p3, reg16_ld_14_p4
  assign DOUT15__0 = CS15 ? reg16_ld_14_p3 : 16'bz;  // Controlled_Buffer controlled_buffer_16
  and and_13 (reg16_ld_11_p4, CS9, WR);
  and and_14 (reg16_ld_12_p4, CS11, WR);
  and and_15 (reg16_ld_13_p4, CS13, WR);
  and and_16 (reg16_ld_14_p4, CS15, WR);
  // REG16_LD reg16_ld_15: pin names not known; wires that end beside it: CLK, DIN15__0, reg16_ld_15_p3, reg16_ld_15_p4
  assign DOUT15__0 = CS16 ? reg16_ld_15_p3 : 16'bz;  // Controlled_Buffer controlled_buffer_17
  // REG16_LD reg16_ld_16: pin names not known; wires that end beside it: CLK, DIN15__0, reg16_ld_16_p3, reg16_ld_16_p4
  assign DOUT15__0 = CS18 ? reg16_ld_16_p3 : 16'bz;  // Controlled_Buffer controlled_buffer_18
  // REG16_LD reg16_ld_17: pin names not known; wires that end beside it: CLK, DIN15__0, reg16_ld_17_p3, reg16_ld_17_p4
  assign DOUT15__0 = CS20 ? reg16_ld_17_p3 : 16'bz;  // Controlled_Buffer controlled_buffer_19
  // REG16_LD reg16_ld_18: pin names not known; wires that end beside it: CLK, DIN15__0, reg16_ld_18_p3, reg16_ld_18_p4
  assign DOUT15__0 = CS22 ? reg16_ld_18_p3 : 16'bz;  // Controlled_Buffer controlled_buffer_20
  and and_17 (reg16_ld_15_p4, CS16, WR);
  and and_18 (reg16_ld_16_p4, CS18, WR);
  and and_19 (reg16_ld_17_p4, CS20, WR);
  and and_20 (reg16_ld_18_p4, CS22, WR);
  // REG16_LD reg16_ld_19: pin names not known; wires that end beside it: CLK, DIN15__0, reg16_ld_19_p3, reg16_ld_19_p4
  assign DOUT15__0 = CS17 ? reg16_ld_19_p3 : 16'bz;  // Controlled_Buffer controlled_buffer_21
  // REG16_LD reg16_ld_20: pin names not known; wires that end beside it: CLK, DIN15__0, reg16_ld_20_p3, reg16_ld_20_p4
  assign DOUT15__0 = CS19 ? reg16_ld_20_p3 : 16'bz;  // Controlled_Buffer controlled_buffer_22
  // REG16_LD reg16_ld_21: pin names not known; wires that end beside it: CLK, DIN15__0, reg16_ld_21_p3, reg16_ld_21_p4
  assign DOUT15__0 = CS21 ? reg16_ld_21_p3 : 16'bz;  // Controlled_Buffer controlled_buffer_23
  // REG16_LD reg16_ld_22: pin names not known; wires that end beside it: CLK, DIN15__0, reg16_ld_22_p3, reg16_ld_22_p4
  assign DOUT15__0 = CS23 ? reg16_ld_22_p3 : 16'bz;  // Controlled_Buffer controlled_buffer_24
  and and_21 (reg16_ld_19_p4, CS17, WR);
  and and_22 (reg16_ld_20_p4, CS19, WR);
  and and_23 (reg16_ld_21_p4, CS21, WR);
  and and_24 (reg16_ld_22_p4, CS23, WR);
  // REG16_LD reg16_ld_23: pin names not known; wires that end beside it: CLK, DIN15__0, reg16_ld_23_p3, reg16_ld_23_p4
  assign DOUT15__0 = CS24 ? reg16_ld_23_p3 : 16'bz;  // Controlled_Buffer controlled_buffer_25
  // REG16_LD reg16_ld_24: pin names not known; wires that end beside it: CLK, DIN15__0, reg16_ld_24_p3, reg16_ld_24_p4
  assign DOUT15__0 = CS26 ? reg16_ld_24_p3 : 16'bz;  // Controlled_Buffer controlled_buffer_26
  // REG16_LD reg16_ld_25: pin names not known; wires that end beside it: CLK, DIN15__0, reg16_ld_25_p3, reg16_ld_25_p4
  assign DOUT15__0 = CS28 ? reg16_ld_25_p3 : 16'bz;  // Controlled_Buffer controlled_buffer_27
  // REG16_LD reg16_ld_26: pin names not known; wires that end beside it: CLK, DIN15__0, reg16_ld_26_p3, reg16_ld_26_p4
  assign DOUT15__0 = CS30 ? reg16_ld_26_p3 : 16'bz;  // Controlled_Buffer controlled_buffer_28
  and and_25 (reg16_ld_23_p4, CS24, WR);
  and and_26 (reg16_ld_24_p4, CS26, WR);
  and and_27 (reg16_ld_25_p4, CS28, WR);
  and and_28 (reg16_ld_26_p4, CS30, WR);
  // REG16_LD reg16_ld_27: pin names not known; wires that end beside it: CLK, DIN15__0, reg16_ld_27_p3, reg16_ld_27_p4
  assign DOUT15__0 = CS25 ? reg16_ld_27_p3 : 16'bz;  // Controlled_Buffer controlled_buffer_29
  // REG16_LD reg16_ld_28: pin names not known; wires that end beside it: CLK, DIN15__0, reg16_ld_28_p3, reg16_ld_28_p4
  assign DOUT15__0 = CS27 ? reg16_ld_28_p3 : 16'bz;  // Controlled_Buffer controlled_buffer_30
  // REG16_LD reg16_ld_29: pin names not known; wires that end beside it: CLK, DIN15__0, reg16_ld_29_p3, reg16_ld_29_p4
  assign DOUT15__0 = CS29 ? reg16_ld_29_p3 : 16'bz;  // Controlled_Buffer controlled_buffer_31
  // REG16_LD reg16_ld_30: pin names not known; wires that end beside it: CLK, DIN15__0, reg16_ld_30_p3, reg16_ld_30_p4
  assign DOUT15__0 = CS31 ? reg16_ld_30_p3 : 16'bz;  // Controlled_Buffer controlled_buffer_32
  and and_29 (reg16_ld_27_p4, CS25, WR);
  and and_30 (reg16_ld_28_p4, CS27, WR);
  and and_31 (reg16_ld_29_p4, CS29, WR);
  and and_32 (reg16_ld_30_p4, CS31, WR);

  // Other names for the same wires on the sheet: A3__0[3:0] = A4__0[3:0]; A4 = A4__0[4]; decA = in_4; incA = in_1;
  //   incPC = in_9; inREG[15:0] = DIN15__0; ldA = in_3; ldPC = in_2; outREG[15:0] = DOUT15__0
endmodule

module ROM32x24 (
  input  [4:0] A7__0,
  input  CS,
  output [23:0] OUT
);

  ROM #(.addrWidth(5), .dataWidth(24)) rom_1 (.addr(A7__0), .data(OUT), .sel(CS));
endmodule

module ALU16_ADD_SUB (
  input  [15:0] A15__0,
  input  [15:0] B15__0,
  input  Cin,
  input  add,
  input  sub,
  output Cout,
  output [15:0] ALU15__0
);

  wire alu8_add_sub_1_p5;

  // ALU8_ADD_SUB alu8_add_sub_1: pin names not known; wires that end beside it: Cout, A15__0[15:8], ALU15__0[15:8], B15__0[15:8], alu8_add_sub_1_p5, add, sub
  // ALU8_ADD_SUB alu8_add_sub_2: pin names not known; wires that end beside it: alu8_add_sub_1_p5, A15__0[7:0], ALU15__0[7:0], B15__0[7:0], Cin, add, sub
endmodule

module ROM64x46 (
  input  [5:0] A5__0,
  input  CS,
  output [31:0] DOUT31__0,
  output [13:0] DOUT45__32
);

  ROM #(.addrWidth(6), .dataWidth(14)) rom_1 (.addr(A5__0), .data(DOUT45__32), .sel(CS));
  ROM #(.addrWidth(6), .dataWidth(32)) rom_2 (.addr(A5__0), .data(DOUT31__0), .sel(CS));
endmodule

module ROM16x24 (
  input  [3:0] A3__0,
  input  CS,
  output [23:0] DOUT
);

  ROM #(.addrWidth(4), .dataWidth(24)) rom_1 (.addr(A3__0), .data(DOUT), .sel(CS));
endmodule

module REG6_INC_CL (
  input  INC,
  input  mr,
  input  CL,
  input  CLK,
  output [5:0] A5__0
);

  wire reg2m_cl_inc_1_p6, reg2m_cl_inc_2_p7;

  // REG2m_CL_INC reg2m_cl_inc_1: pin names not known; wires that end beside it: CL, CLK, mr, A5__0[5:4], INC, reg2m_cl_inc_1_p6
  // REG2m_CL_INC reg2m_cl_inc_2: pin names not known; wires that end beside it: CL, CLK, reg2m_cl_inc_1_p6, mr, A5__0[3:2], INC, reg2m_cl_inc_2_p7
  // REG2m_CL_INC reg2m_cl_inc_3: pin names not known; wires that end beside it: CL, CLK, reg2m_cl_inc_2_p7, mr, A5__0[1:0], INC, INC

  // Notes on the sheet:
  //   __
endmodule
