// Logisim project ORT2Project.circ as structural Verilog: 8 circuits, main circuit COMPUTER
module COMPUTER (
);

  wire BTN_INTR0_out, BTN_INTR1_out, BTN_INTR2_out, BTN_INTR3_out, BTN_INTR4_out, BTN_INTR5_out,
       BTN_INTR6_out, BTN_INTR7_out, BTN_RST_out, CLK, cpu_1_inta, pull_resistor_3_node,
       pull_resistor_6_node, ram_1_out_8, rst;
  wire [2:0] cpu_1_uext2__0;
  wire [7:0] interrupt_interface_8_1_intr7__0;
  wire [15:0] pull_resistor_1_node, pull_resistor_2_node, ram_1_out_7;

  Button BTN_RST (.out(BTN_RST_out));
  Clock u_CLK (.out(CLK));
  // RisingEdge risingedge_1: pin names not known; wires that end beside it: BTN_RST_out, CLK, rst
  RAM ram_1 (
    .in_1(pull_resistor_1_node), .in_2(CLK), .in_3(pull_resistor_2_node), .in_4(pull_resistor_3_node),
    .in_5(pull_resistor_6_node), .in_6(rst), .out_7(ram_1_out_7), .out_8(ram_1_out_8));
  Pull_Resistor pull_resistor_1 (.node(pull_resistor_1_node));
  Pull_Resistor pull_resistor_2 (.node(pull_resistor_2_node));
  Pull_Resistor pull_resistor_3 (.node(pull_resistor_3_node));
  Pull_Resistor pull_resistor_4 (.node(ram_1_out_7));
  Pull_Resistor pull_resistor_5 (.node(ram_1_out_8));
  Pull_Resistor pull_resistor_6 (.node(pull_resistor_6_node));
  CPU cpu_1 (
    .in_1(rst), .in_2(CLK), .in_3(ram_1_out_8), .in_4(ram_1_out_7), .ABUS(pull_resistor_1_node),
    .DOUTBUS(pull_resistor_2_node), .out_8(pull_resistor_3_node), .out_9(pull_resistor_6_node),
    .inta(cpu_1_inta), .UEXT2__0(cpu_1_uext2__0), .intr3__0(interrupt_interface_8_1_intr7__0));
  INTERRUPT_INTERFACE_8 interrupt_interface_8_1 (
    .BTN_INTR0(BTN_INTR0_out), .BTN_INTR1(BTN_INTR1_out), .BTN_INTR2(BTN_INTR2_out),
    .BTN_INTR3(BTN_INTR3_out), .BTN_INTR4(BTN_INTR4_out), .BTN_INTR5(BTN_INTR5_out),
    .BTN_INTR6(BTN_INTR6_out), .BTN_INTR7(BTN_INTR7_out), .inta(cpu_1_inta), .UEXT2__0(cpu_1_uext2__0),
    .CLK(CLK), .intr7__0(interrupt_interface_8_1_intr7__0));
  Button BTN_INTR7 (.out(BTN_INTR7_out));
  Button BTN_INTR6 (.out(BTN_INTR6_out));
  Button BTN_INTR5 (.out(BTN_INTR5_out));
  Button BTN_INTR4 (.out(BTN_INTR4_out));
  Button BTN_INTR3 (.out(BTN_INTR3_out));
  Button BTN_INTR2 (.out(BTN_INTR2_out));
  Button BTN_INTR1 (.out(BTN_INTR1_out));
  Button BTN_INTR0 (.out(BTN_INTR0_out));
endmodule

module CPU (
  input  in_1,
  input  in_2,
  input  in_3,
  input  [15:0] in_4,
  input  [7:0] intr3__0,
  output [15:0] ABUS,
  output [15:0] DOUTBUS,
  output out_8,
  output out_9,
  output inta,
  output [2:0] UEXT2__0
);

  wire C16, grinst, SC32, SCN;
  wire [3:0] common_1_phaseffbus;
  wire [5:0] common_1_addrbus;
  wire [6:0] pull_resistor_3_node;
  wire [7:0] pull_resistor_4_node;
  wire [15:0] ALU, B, GPR15__0, INTRADDR, PSW;
  wire [18:0] pull_resistor_6_node;
  wire [19:0] common_1_instrucbus, pull_resistor_5_node;

  COMMON common_1 (
    .CLK(in_2), .RST(in_1), .DIN(in_4), .CMEMBUS(pull_resistor_5_node), .MAR(ABUS), .MDR(DOUTBUS),
    .PHASEFFBUS(common_1_phaseffbus), .INSTRUCBUS(common_1_instrucbus), .ADDRBUS(common_1_addrbus),
    .PSW(PSW), .CREGBUS(pull_resistor_6_node), .CFFBUS(pull_resistor_4_node), .B(B),
    .CPSW(pull_resistor_3_node), .ALU(ALU), .IVTPPDSP(INTRADDR), .grinst(grinst), .GPR(GPR15__0), .C16(C16),
    .out_14(SCN), .out_15(SC32));
  Pull_Resistor pull_resistor_1 (.node(common_1_phaseffbus));
  Pull_Resistor pull_resistor_2 (.node(common_1_instrucbus));
  Pull_Resistor pull_resistor_3 (.node(pull_resistor_3_node));
  Pull_Resistor pull_resistor_4 (.node(pull_resistor_4_node));
  Pull_Resistor pull_resistor_5 (.node(pull_resistor_5_node));
  Pull_Resistor pull_resistor_6 (.node(pull_resistor_6_node));
  Pull_Resistor pull_resistor_7 (.node(common_1_addrbus));
  FETCH fetch_1 (
    .in_1(in_1), .in_2(in_2), .in_3(in_3), .PHASEFFBUS(common_1_phaseffbus),
    .INSTRUCBUS(common_1_instrucbus), .ADDRBUS(common_1_addrbus), .PSW(PSW), .rdMEM(out_9),
    .CMEMBUS(pull_resistor_5_node), .CFFBUS(pull_resistor_4_node), .CREGBUS(pull_resistor_6_node),
    .in_4(grinst));
  ADDR addr_1 (
    .in_1(in_1), .in_2(in_2), .in_3(in_3), .PHASEFFBUS(common_1_phaseffbus),
    .INSTRUCBUS(common_1_instrucbus), .ADDRBUS(common_1_addrbus), .rdMEM(out_9),
    .CMEMBUS(pull_resistor_5_node), .CFFBUS(pull_resistor_4_node), .CREGBUS(pull_resistor_6_node));
  EXEC exec_1 (
    .in_3(in_1), .in_4(in_2), .in_5(in_3), .B(B), .PHASEFFBUS(common_1_phaseffbus),
    .INSTRUCBUS(common_1_instrucbus), .ADDRBUS(common_1_addrbus), .PSW(PSW), .ALU(ALU),
    .CMEMBUS(pull_resistor_5_node), .CFFBUS(pull_resistor_4_node), .CREGBUS(pull_resistor_6_node),
    .CPSW(pull_resistor_3_node), .rdMEM(out_9), .wrMEM(out_8), .out_12(C16), .GPR(GPR15__0), .in_1(SCN),
    .in_2(SC32));
  INTR intr_1 (
    .in_1(in_1), .in_2(in_2), .in_3(in_3), .PHASEFFBUS(common_1_phaseffbus),
    .INSTRUCBUS(common_1_instrucbus), .PSW(PSW), .intr(intr3__0), .ADDIVTP(INTRADDR),
    .CMEMBUS(pull_resistor_5_node), .CFFBUS(pull_resistor_4_node), .CREGBUS(pull_resistor_6_node),
    .rdMEM(out_9), .wrMEM(out_8), .UEXT2__0(UEXT2__0), .inta(inta));

  // Other names for the same wires on the sheet: CLK = in_2; DIN15__0[15:0] = in_4; FCBUS = in_3;
  //   intr7__0[7:0] = intr3__0; MAR[15:0] = ABUS; MDR[15:0] = DOUTBUS; RD = out_9; rst = in_1; WR = out_8
endmodule

module COMMON (
  input  CLK,
  input  C16,
  input  RST,
  input  [15:0] DIN,
  input  [15:0] ALU,
  input  [15:0] IVTPPDSP,
  input  [19:0] CMEMBUS,
  input  [7:0] CFFBUS,
  input  [18:0] CREGBUS,
  input  [6:0] CPSW,
  output [15:0] MAR,
  output [15:0] MDR,
  output [15:0] GPR,
  output out_14,
  output out_15,
  output [3:0] PHASEFFBUS,
  output [19:0] INSTRUCBUS,
  output [5:0] ADDRBUS,
  output [15:0] PSW,
  output grinst,
  output [15:0] B
);

  wire ADC, adrInstrukcije, ADRZ, and_1_out, and_2_out, and_3_out, and_4_out, and_5_out, and_6_out,
       and_7_out, and_8_out, and_9_out, and_10_out, and_11_out, and_12_out, and_13_out, and_14_out,
       and_15_out, and_16_out, and_17_out, and_18_out, and_19_out, and_20_out, and_22_out, and_23_out,
       and_24_out, and_25_out, and_26_out, and_27_out, and_28_out, and_30_out, and_31_out, and_32_out,
       and_33_out, and_34_out, and_35_out, and_36_out, and_37_out, bezadresneInsrtukcije, bezuslovniSkok,
       dc4_16_1_p6, dc4_16_1_p8, dc4_16_1_p9, dc4_16_1_p10, dc4_16_1_p11, dc4_16_1_p12, dc4_16_1_p13,
       dc4_16_1_p14, dc4_16_1_p15, dc4_16_1_p16, dc4_16_1_p17, dc4_16_1_p18, dc4_16_2_p3, dc4_16_2_p4,
       dc4_16_2_p5, dc4_16_2_p8, dc4_16_2_p9, dc4_16_2_p10, dc4_16_2_p12, dc4_16_2_p13, dc4_16_2_p14,
       dc4_16_2_p16, dc4_16_2_p17, dc4_16_2_p18, dc4_16_3_p3, dc4_16_3_p4, dc4_16_3_p5, dc4_16_3_p6,
       dc4_16_3_p7, dc4_16_3_p8, dc4_16_3_p9, dc4_16_3_p10, dc4_16_3_p11, dc4_16_3_p12, dc4_16_3_p13,
       dc4_16_3_p14, dc4_16_3_p15, dc4_16_3_p16, dc4_16_3_p17, dc4_16_3_p18, dc4_16_4_p10, dc4_16_4_p11,
       dc4_16_4_p12, dc4_16_4_p13, dc4_16_4_p14, dc4_16_4_p15, dc4_16_4_p16, dc4_16_4_p17, dc4_16_4_p18,
       dc4_16_5_p4, dc4_16_5_p5, dc4_16_5_p6, dc4_16_5_p7, dc4_16_5_p8, dc4_16_5_p9, dc4_16_5_p10,
       dc4_16_5_p11, dc4_16_5_p12, dc4_16_5_p13, dc4_16_5_p14, dc4_16_5_p15, dc4_16_5_p16, dc4_16_5_p17,
       dc4_16_5_p18, dc4_16_6_p4, dc4_16_6_p5, dc4_16_6_p6, dc4_16_6_p7, dc4_16_6_p8, dc4_16_6_p9,
       dc4_16_6_p10, dc4_16_6_p11, dc4_16_6_p12, dc4_16_6_p13, dc4_16_6_p14, dc4_16_6_p15, dc4_16_6_p16,
       dc4_16_6_p17, dc4_16_6_p18, dc4_16_7_p5, dc4_16_7_p6, dc4_16_7_p7, dc4_16_7_p8, dc4_16_7_p9,
       dc4_16_7_p10, dc4_16_7_p11, dc4_16_7_p12, dc4_16_7_p13, dc4_16_7_p14, dc4_16_7_p15, dc4_16_7_p16,
       dc4_16_7_p17, dc4_16_7_p18, dc4_16_8_p8, dc4_16_8_p10, dc4_16_8_p11, dc4_16_8_p12, dc4_16_8_p13,
       dc4_16_8_p14, dc4_16_8_p15, dc4_16_8_p16, dc4_16_8_p17, dc4_16_8_p18, g0, g1, g2, g3, g4, g5, g6,
       IR20, IR23, mp4_16b_1_p5, mp4_16b_2_p5, mp4_16b_3_p5, mp8_16b_1_p8, not_1_out, not_5_out, not_9_out,
       or_13_out, or_16_out, or_17_out, or_18_out, or_19_out, or_20_out, or_21_out, or_22_out, or_23_out,
       or_24_out, or_25_out, or_26_out, or_27_out, rsff_2_p4, rsff_3_p4, rsff_4_p4, rsff_6_p4, rsff_7_p4,
       rsff_8_p4, rsff_10_p4, uslovniSkok;
  wire [1:0] IR22__21;
  wire [3:0] IR19__16, IR27__24;
  wire [4:0] SCN5__0;
  wire [5:0] SC5__0;
  wire [7:0] mp4_8b_1_p8;
  wire [9:0] reg16_4_p3;
  wire [15:0] ADDADDR, ADDRIP, IR15__0, mp8_16b_2_p8, SC15__0, SP15__0;
  wire [15:12] IR31__16;

  or or_1 (ADRZ, INSTRUCBUS[12], INSTRUCBUS[14], INSTRUCBUS[15], INSTRUCBUS[3]);
  or or_2 (ADC, INSTRUCBUS[14], INSTRUCBUS[15], INSTRUCBUS[16]);
  // DC4_16 dc4_16_1: pin names not known; wires that end beside it: IR27__24, uslovniSkok, INSTRUCBUS[6], INSTRUCBUS[7], INSTRUCBUS[8], dc4_16_1_p6, INSTRUCBUS[9], dc4_16_1_p8, dc4_16_1_p9, dc4_16_1_p10, dc4_16_1_p11, dc4_16_1_p12, dc4_16_1_p13, dc4_16_1_p14, dc4_16_1_p15, dc4_16_1_p16, dc4_16_1_p17, dc4_16_1_p18
  // MP8_16b mp8_16b_1: pin names not known; wires that end beside it: CMEMBUS[3], CMEMBUS[4], CMEMBUS[5], GPR, IR15__0, B, ADDRIP, mp8_16b_1_p8, SP15__0, IVTPPDSP, 1'b1
  // REG16_INC_LD reg16_inc_ld_1: pin names not known; wires that end beside it: CLK, mp8_16b_1_p8, MAR, CMEMBUS[0], CMEMBUS[1]
  // REG16_LD reg16_ld_1: pin names not known; wires that end beside it: CLK, MDR, {IR31__16, IR27__24, IR23, IR22__21, IR20, IR19__16}, CREGBUS[0]
  // DC4_16 dc4_16_2: pin names not known; wires that end beside it: IR31__16, PSW[0], dc4_16_2_p3, dc4_16_2_p4, dc4_16_2_p5, adrInstrukcije, bezuslovniSkok, dc4_16_2_p8, dc4_16_2_p9, dc4_16_2_p10, bezadresneInsrtukcije, dc4_16_2_p12, dc4_16_2_p13, dc4_16_2_p14, uslovniSkok, dc4_16_2_p16, dc4_16_2_p17, dc4_16_2_p18
  // MP4_16b mp4_16b_1: pin names not known; wires that end beside it: CREGBUS[14], CREGBUS[15], MDR, IR15__0, mp4_16b_1_p5, GPR, MAR, 1'b1
  // REG16 reg16_1: pin names not known; wires that end beside it: CREGBUS[13], CLK, mp4_16b_1_p5, B, CREGBUS[10], CREGBUS[11], CREGBUS[12]
  or or_3 (g4, dc4_16_1_p6, dc4_16_1_p8, dc4_16_1_p9, dc4_16_1_p10, dc4_16_1_p11, dc4_16_1_p12, dc4_16_1_p13, dc4_16_1_p14, dc4_16_1_p15, dc4_16_1_p16, dc4_16_1_p17, dc4_16_1_p18);
  // DC4_16 dc4_16_3: pin names not known; wires that end beside it: {IR23, IR22__21, IR20}, adrInstrukcije, dc4_16_3_p3, dc4_16_3_p4, dc4_16_3_p5, dc4_16_3_p6, dc4_16_3_p7, dc4_16_3_p8, dc4_16_3_p9, dc4_16_3_p10, dc4_16_3_p11, dc4_16_3_p12, dc4_16_3_p13, dc4_16_3_p14, dc4_16_3_p15, dc4_16_3_p16, dc4_16_3_p17, dc4_16_3_p18
  or or_4 (g0, dc4_16_2_p3, dc4_16_2_p4, dc4_16_2_p5, dc4_16_2_p8, dc4_16_2_p9, dc4_16_2_p10, dc4_16_2_p12, dc4_16_2_p13, dc4_16_2_p14, dc4_16_2_p16, dc4_16_2_p17, dc4_16_2_p18);
  // MP4_16b mp4_16b_2: pin names not known; wires that end beside it: CMEMBUS[11], CMEMBUS[6], DIN, GPR, mp4_16b_2_p5, {PSW[15], {10{1'b0}}, PSW[4:0]}, 1'b1
  // REG16_LD reg16_ld_2: pin names not known; wires that end beside it: CLK, mp4_16b_2_p5, MDR, CMEMBUS[2]
  // REG16_LD reg16_ld_3: pin names not known; wires that end beside it: CLK, MDR, IR15__0, CREGBUS[1]
  // DC4_16 dc4_16_4: pin names not known; wires that end beside it: IR27__24, adrInstrukcije, INSTRUCBUS[12], INSTRUCBUS[13], INSTRUCBUS[14], INSTRUCBUS[15], INSTRUCBUS[16], INSTRUCBUS[17], INSTRUCBUS[18], dc4_16_4_p10, dc4_16_4_p11, dc4_16_4_p12, dc4_16_4_p13, dc4_16_4_p14, dc4_16_4_p15, dc4_16_4_p16, dc4_16_4_p17, dc4_16_4_p18
  or or_5 (ADDRBUS[2], dc4_16_3_p5, dc4_16_3_p6);
  or or_6 (ADDRBUS[3], dc4_16_3_p7, dc4_16_3_p8);
  or or_7 (ADDRBUS[4], dc4_16_3_p9, dc4_16_3_p10);
  or or_8 (ADDRBUS[5], dc4_16_3_p11, dc4_16_3_p12, dc4_16_3_p13, dc4_16_3_p14, dc4_16_3_p15, dc4_16_3_p16, dc4_16_3_p17, dc4_16_3_p18);
  // REG16 reg16_2: pin names not known; wires that end beside it: CLK, 16'hf000, SP15__0, RST, CMEMBUS[9], CMEMBUS[10]
  // ADD16 add16_1: pin names not known; wires that end beside it: C16, {{15{IR22__21[1]}}, IR22__21[0]}, ADDRIP, GPR, 1'b0
  // DC4_16 dc4_16_5: pin names not known; wires that end beside it: IR19__16, dc4_16_3_p3, ADDRBUS[0], dc4_16_5_p4, dc4_16_5_p5, dc4_16_5_p6, dc4_16_5_p7, dc4_16_5_p8, dc4_16_5_p9, dc4_16_5_p10, dc4_16_5_p11, dc4_16_5_p12, dc4_16_5_p13, dc4_16_5_p14, dc4_16_5_p15, dc4_16_5_p16, dc4_16_5_p17, dc4_16_5_p18
  or or_9 (g1, dc4_16_4_p10, dc4_16_4_p11, dc4_16_4_p12, dc4_16_4_p13, dc4_16_4_p14, dc4_16_4_p15, dc4_16_4_p16, dc4_16_4_p17, dc4_16_4_p18);
  // DC4_16 dc4_16_6: pin names not known; wires that end beside it: IR19__16, dc4_16_3_p4, ADDRBUS[1], dc4_16_6_p4, dc4_16_6_p5, dc4_16_6_p6, dc4_16_6_p7, dc4_16_6_p8, dc4_16_6_p9, dc4_16_6_p10, dc4_16_6_p11, dc4_16_6_p12, dc4_16_6_p13, dc4_16_6_p14, dc4_16_6_p15, dc4_16_6_p16, dc4_16_6_p17, dc4_16_6_p18
  // DC4_16 dc4_16_7: pin names not known; wires that end beside it: IR27__24, bezuslovniSkok, INSTRUCBUS[10], INSTRUCBUS[11], dc4_16_7_p5, dc4_16_7_p6, dc4_16_7_p7, dc4_16_7_p8, dc4_16_7_p9, dc4_16_7_p10, dc4_16_7_p11, dc4_16_7_p12, dc4_16_7_p13, dc4_16_7_p14, dc4_16_7_p15, dc4_16_7_p16, dc4_16_7_p17, dc4_16_7_p18
  or or_10 (g5, dc4_16_5_p4, dc4_16_5_p5, dc4_16_5_p6, dc4_16_5_p7, dc4_16_5_p8, dc4_16_5_p9, dc4_16_5_p10, dc4_16_5_p11, dc4_16_5_p12, dc4_16_5_p13, dc4_16_5_p14, dc4_16_5_p15, dc4_16_5_p16, dc4_16_5_p17, dc4_16_5_p18);
  // MP4_8b mp4_8b_1: pin names not known; wires that end beside it: 8'h2, 8'h1, {8{1'b0}}, {IR23, IR22__21, IR20, IR19__16}, CREGBUS[8], 1'b1, CREGBUS[9], mp4_8b_1_p8
  or or_11 (g2, dc4_16_7_p5, dc4_16_7_p6, dc4_16_7_p7, dc4_16_7_p8, dc4_16_7_p9, dc4_16_7_p10, dc4_16_7_p11, dc4_16_7_p12, dc4_16_7_p13, dc4_16_7_p14, dc4_16_7_p15, dc4_16_7_p16, dc4_16_7_p17, dc4_16_7_p18);
  or or_12 (g6, dc4_16_6_p4, dc4_16_6_p5, dc4_16_6_p6, dc4_16_6_p7, dc4_16_6_p8, dc4_16_6_p9, dc4_16_6_p10, dc4_16_6_p11, dc4_16_6_p12, dc4_16_6_p13, dc4_16_6_p14, dc4_16_6_p15, dc4_16_6_p16, dc4_16_6_p17, dc4_16_6_p18);
  // ADD16 add16_2: pin names not known; wires that end beside it: C16, {{9{IR23}}, IR22__21, IR20, IR19__16}, ADDADDR, GPR, 1'b0
  not not_1 (not_1_out, RST);
  // RSFF rsff_1: pin names not known; wires that end beside it: CFFBUS[1], CLK, CFFBUS[0], not_1_out, PHASEFFBUS[0]
  // DC4_16 dc4_16_8: pin names not known; wires that end beside it: IR27__24, bezadresneInsrtukcije, INSTRUCBUS[0], INSTRUCBUS[1], INSTRUCBUS[2], INSTRUCBUS[3], INSTRUCBUS[4], dc4_16_8_p8, INSTRUCBUS[5], dc4_16_8_p10, dc4_16_8_p11, dc4_16_8_p12, dc4_16_8_p13, dc4_16_8_p14, dc4_16_8_p15, dc4_16_8_p16, dc4_16_8_p17, dc4_16_8_p18
  or or_13 (or_13_out, INSTRUCBUS[13], INSTRUCBUS[17]);
  and and_1 (and_1_out, INSTRUCBUS[17], ADDRBUS[2]);
  // MP8_16b mp8_16b_2: pin names not known; wires that end beside it: CREGBUS[16], CREGBUS[5], CREGBUS[6], B, IR15__0, MDR, MAR, mp8_16b_2_p8, ALU, ADDADDR, 1'b1
  GPR32x16 gpr32x16_1 (
    .DIN15__0(mp8_16b_2_p8), .rst(RST), .WR(CREGBUS[7]), .CLK(CLK), .A4__0(mp4_8b_1_p8[4:0]),
    .DOUT15__0(GPR), .in_9(CMEMBUS[7]), .in_3(CREGBUS[2]), .in_4(CREGBUS[4]), .in_2(CMEMBUS[8]),
    .in_1(CREGBUS[3]));
  or or_14 (grinst, g0, g1, g2, g3, g4, g5, g6, or_16_out);
  and and_2 (and_2_out, or_13_out, ADDRBUS[0]);
  // MP4_16b mp4_16b_3: pin names not known; wires that end beside it: CREGBUS[14], CREGBUS[15], MDR, IR15__0, mp4_16b_3_p5, GPR, MAR, 1'b1
  // REG16 reg16_3: pin names not known; wires that end beside it: CREGBUS[13], CLK, mp4_16b_3_p5, SC15__0, CREGBUS[10], CREGBUS[11], CREGBUS[12]
  or or_15 (g3, dc4_16_8_p8, dc4_16_8_p10, dc4_16_8_p11, dc4_16_8_p12, dc4_16_8_p13, dc4_16_8_p14, dc4_16_8_p15, dc4_16_8_p16, dc4_16_8_p17, dc4_16_8_p18);
  or or_16 (or_16_out, and_2_out, and_1_out);
  // RSFF rsff_2: pin names not known; wires that end beside it: CFFBUS[3], CLK, CFFBUS[2], rsff_2_p4, PHASEFFBUS[1]
  not not_2 (rsff_2_p4, RST);
  or or_17 (or_17_out, INSTRUCBUS[16], INSTRUCBUS[15]);
  and and_3 (and_3_out, MAR[3], INSTRUCBUS[2]);
  and and_4 (and_4_out, ADRZ, and_5_out);
  and and_5 (and_5_out, ~GPR[0], ~GPR[1], ~GPR[2], ~GPR[3], ~GPR[4], ~GPR[5], ~GPR[6], ~GPR[7], ~GPR[8], ~GPR[9], ~GPR[10], ~GPR[11], ~GPR[12], ~GPR[13], ~GPR[14], ~GPR[15]);  // AND_Gate
  and and_6 (and_6_out, ~ALU[15], B[15], GPR[15]);  // AND_Gate
  and and_7 (and_7_out, ALU[15], ~B[15], ~GPR[15]);  // AND_Gate
  and and_8 (and_8_out, ~ALU[15], ~B[15], GPR[15]);  // AND_Gate
  and and_9 (and_9_out, ALU[15], B[15], ~GPR[15]);  // AND_Gate
  and and_10 (and_10_out, MAR[2], INSTRUCBUS[2]);
  and and_11 (and_11_out, INSTRUCBUS[3], C16);
  and and_12 (and_12_out, INSTRUCBUS[14], C16);
  and and_13 (and_13_out, or_17_out, ~C16);  // AND_Gate
  // REG16 reg16_4: pin names not known; wires that end beside it: CLK, 16'h1f, {reg16_4_p3, out_14, SCN5__0}, CMEMBUS[14], CMEMBUS[15]
  // RSFF rsff_3: pin names not known; wires that end beside it: CFFBUS[5], CLK, CFFBUS[4], rsff_3_p4, PHASEFFBUS[2]
  not not_3 (rsff_3_p4, RST);
  or or_18 (or_18_out, and_3_out, and_4_out, and_14_out);
  and and_14 (and_14_out, INSTRUCBUS[16], and_22_out);
  and and_15 (and_15_out, MAR[4], INSTRUCBUS[2]);
  and and_16 (and_16_out, ADRZ, GPR[15]);
  and and_17 (and_17_out, ALU[15], INSTRUCBUS[16]);
  and and_18 (and_18_out, MAR[4], INSTRUCBUS[2]);
  and and_19 (and_19_out, INSTRUCBUS[14], or_19_out);
  or or_19 (or_19_out, and_6_out, and_7_out);
  or or_20 (or_20_out, INSTRUCBUS[16], INSTRUCBUS[15]);
  or or_21 (or_21_out, and_8_out, and_9_out);
  or or_22 (or_22_out, and_11_out, and_12_out, and_13_out);
  and and_20 (and_20_out, ~MAR[0], INSTRUCBUS[2], CPSW[1]);  // AND_Gate
  // AND_Gate and_21 has open pins: in0=MAR[0], in1=INSTRUCBUS[2], in2=CPSW[1], out=open
  and and_22 (and_22_out, ~ALU[0], ~ALU[1], ~ALU[2], ~ALU[3], ~ALU[4], ~ALU[5], ~ALU[6], ~ALU[7], ~ALU[8], ~ALU[9], ~ALU[10], ~ALU[11], ~ALU[12], ~ALU[13], ~ALU[14], ~ALU[15]);  // AND_Gate
  or or_23 (or_23_out, and_15_out, and_16_out, and_17_out);
  or or_24 (or_24_out, and_18_out, or_25_out);
  or or_25 (or_25_out, and_19_out, and_23_out, and_27_out);
  and and_23 (and_23_out, or_20_out, or_21_out);
  and and_24 (and_24_out, MAR[15], INSTRUCBUS[2]);
  or or_26 (or_26_out, and_10_out, or_22_out);
  or or_27 (or_27_out, and_20_out, CPSW[0]);
  and and_25 (and_25_out, ~or_18_out, CPSW[3]);  // AND_Gate
  and and_26 (and_26_out, or_18_out, CPSW[3]);
  and and_27 (and_27_out, INSTRUCBUS[3], and_28_out);
  and and_28 (and_28_out, ~ALU[15], GPR[15]);  // AND_Gate
  REG6_INC_CL reg6_inc_cl_1 (.INC(CMEMBUS[13]), .CLK(CLK), .A5__0(SC5__0), .CL(CMEMBUS[12]));  // open: mr
  and and_29 (out_15, SC5__0[5], ~SC5__0[4], ~SC5__0[3], ~SC5__0[2], ~SC5__0[1], ~SC5__0[0]);  // AND_Gate
  // RSFF rsff_4: pin names not known; wires that end beside it: CFFBUS[7], CLK, CFFBUS[6], rsff_4_p4, PHASEFFBUS[3]
  not not_4 (rsff_4_p4, RST);
  not not_5 (not_5_out, RST);
  // RSFF rsff_5: pin names not known; wires that end beside it: or_27_out, CLK, not_5_out, PSW[0]
  // RSFF rsff_6: pin names not known; wires that end beside it: and_25_out, CLK, and_26_out, rsff_6_p4, PSW[3]
  not not_6 (rsff_6_p4, RST);
  and and_30 (and_30_out, ~or_23_out, CPSW[2]);  // AND_Gate
  and and_31 (and_31_out, or_23_out, CPSW[2]);
  and and_32 (and_32_out, ~or_24_out, CPSW[5]);  // AND_Gate
  and and_33 (and_33_out, or_24_out, CPSW[5]);
  and and_34 (and_34_out, ~and_24_out, CPSW[6]);  // AND_Gate
  and and_35 (and_35_out, and_24_out, CPSW[6]);
  and and_36 (and_36_out, ~or_26_out, CPSW[4]);  // AND_Gate
  and and_37 (and_37_out, or_26_out, CPSW[4]);
  // RSFF rsff_7: pin names not known; wires that end beside it: and_30_out, CLK, and_31_out, rsff_7_p4, PSW[4]
  not not_7 (rsff_7_p4, RST);
  // RSFF rsff_8: pin names not known; wires that end beside it: and_32_out, CLK, and_33_out, rsff_8_p4, PSW[1]
  not not_8 (rsff_8_p4, RST);
  not not_9 (not_9_out, RST);
  // RSFF rsff_9: pin names not known; wires that end beside it: and_34_out, CLK, and_35_out, not_9_out, PSW[15]
  // RSFF rsff_10: pin names not known; wires that end beside it: and_36_out, CLK, and_37_out, rsff_10_p4, PSW[2]
  not not_10 (rsff_10_p4, RST);

  assign PSW[14:5] = {10{1'b0}};

  // Other names for the same wires on the sheet: IR23__16[7:0] = {IR23, IR22__21, IR20, IR19__16};
  //   IR31__16[11:0] = {IR27__24, IR23, IR22__21, IR20, IR19__16}; SCN = out_14; SCN5__0[5] = out_14;
  //   immed = ADDRBUS[0]; memdir = ADDRBUS[1]; regdir = ADDRBUS[2]; preincr = ADDRBUS[3]; postdec = ADDRBUS[4];
  //   regindpom = ADDRBUS[5]; ALU15__0[15:0] = ALU; B15__0[15:0] = B; stFETCH = CFFBUS[0]; clFETCH = CFFBUS[1];
  //   stADDR = CFFBUS[2]; clADDR = CFFBUS[3]; stEXEC = CFFBUS[4]; clEXEC = CFFBUS[5]; stINTR = CFFBUS[6];
  //   clINTR = CFFBUS[7]; ldMAR = CMEMBUS[0]; incMAR = CMEMBUS[1]; ldMDR = CMEMBUS[2]; mxMAR2 = CMEMBUS[3];
  //   mxMAR1 = CMEMBUS[4]; mxMAR0 = CMEMBUS[5]; mxMDR0 = CMEMBUS[6]; incPC = CMEMBUS[7]; ldPC = CMEMBUS[8];
  //   incSP = CMEMBUS[9]; decSP = CMEMBUS[10]; mxMDR1 = CMEMBUS[11]; clSC = CMEMBUS[12]; incSC = CMEMBUS[13];
  //   ldSCN = CMEMBUS[14]; decSC = CMEMBUS[15]; clPSWSTART = CPSW[0]; ldSTART = CPSW[1]; ldN = CPSW[2]; ldZ = CPSW[3];
  //   ldC = CPSW[4]; ldV = CPSW[5]; ldI = CPSW[6]; ldIR31__16 = CREGBUS[0]; ldIR15__0 = CREGBUS[1]; ldA = CREGBUS[2];
  //   incA = CREGBUS[3]; decA = CREGBUS[4]; mxGPR1 = CREGBUS[5]; mxGPR0 = CREGBUS[6]; wrGPR = CREGBUS[7];
  //   MPGPR1 = CREGBUS[8]; MPGPR0 = CREGBUS[9]; ldB = CREGBUS[10]; incB = CREGBUS[11]; decB = CREGBUS[12];
  //   clB = CREGBUS[13]; mxB1 = CREGBUS[14]; mxB0 = CREGBUS[15]; mxGPR2 = CREGBUS[16]; Din15__0[15:0] = DIN;
  //   ENTRADDR15__0[15:0] = IVTPPDSP; GPR15__0[15:0] = GPR; HALT = INSTRUCBUS[0]; RTS = INSTRUCBUS[1];
  //   RTI = INSTRUCBUS[2]; INC = INSTRUCBUS[3]; PUSHGPR = INSTRUCBUS[4]; POPGPR = INSTRUCBUS[5]; BLEQ = INSTRUCBUS[6];
  //   JEQ = INSTRUCBUS[7]; JGRTU = INSTRUCBUS[8]; JGRT = INSTRUCBUS[9]; JMP = INSTRUCBUS[10]; JSR = INSTRUCBUS[11];
  //   LD = INSTRUCBUS[12]; ST = INSTRUCBUS[13]; ADD = INSTRUCBUS[14]; SUB = INSTRUCBUS[15]; CMP = INSTRUCBUS[16];
  //   JADR = INSTRUCBUS[17]; CLR = INSTRUCBUS[18]; MAR15__0[15:0] = MAR; MDR0 = MAR[0]; MDR1 = MAR[1]; MDR2 = MAR[2];
  //   MDR3 = MAR[3]; MDR4 = MAR[4]; MDR15 = MAR[15]; MDR15__0[15:0] = MDR; FETCH = PHASEFFBUS[0];
  //   ADDR = PHASEFFBUS[1]; EXEC = PHASEFFBUS[2]; INTR = PHASEFFBUS[3]; PSW15__0 (some bits) = {PSW[15], PSW[4:0]};
  //   PSWSTART = PSW[0]; PSWV = PSW[1]; PSWC = PSW[2]; PSWZ = PSW[3]; PSWN = PSW[4]; PSWI = PSW[15]; SC32 = out_15

  // Notes on the sheet:
  //   Instrukcijski registar
  //   Pomocni registri
  //   MAR
  //   Dekoderi za prepoznavanje instrukcije na osnovu sadrzaja registra IR23..16
  //   MDR
  //   PC
  //   FF za pokretanje FETCH, ADDR, EXEC i INTR faze izvršavanja instrukcije
  //   Programska statusna reč (PSW)
endmodule

module FETCH (
  input  in_1,
  input  in_2,
  input  in_3,
  input  in_4,
  input  [3:0] PHASEFFBUS,
  input  [19:0] INSTRUCBUS,
  input  [5:0] ADDRBUS,
  input  [15:0] PSW,
  output [19:0] CMEMBUS,
  output [7:0] CFFBUS,
  output [18:0] CREGBUS,
  output rdMEM
);

  wire adr, adr2, adr4, and_3_out, and_4_out, and_5_out, and_6_out, and_7_out, and_8_out, and_9_out, bezadr2,
       bradr2, brbezadr2, brcnd, brgrinst, brjmp2, brjmp4, brnotFCBUS, bruncnd, clFETCH, incPC, jmp4,
       ldIR15__0, ldIR31__16, ldMAR, ldMDR, MPGPR0, MPGPR1, not_1_out, not_3_out, not_4_out, not_5_out,
       notPSWSTandFETCH, or_5_out, or_6_out, or_7_out, rdMEM_t, reg4_inc_ld_1_p5, reg4_inc_ld_1_p6, stADDR,
       stEXEC;
  wire [3:0] reg4_inc_ld_1_p3, reg4_inc_ld_1_p4;
  wire [15:11] rom16x20_1_dout;

  or or_1 (adr, INSTRUCBUS[12], INSTRUCBUS[13], INSTRUCBUS[14], INSTRUCBUS[15], INSTRUCBUS[16], INSTRUCBUS[17], INSTRUCBUS[18]);
  or or_2 (bezadr2, INSTRUCBUS[0], INSTRUCBUS[1], INSTRUCBUS[2], INSTRUCBUS[3], INSTRUCBUS[4], INSTRUCBUS[5]);
  not not_1 (not_1_out, in_1);
  // REG4_INC_LD reg4_inc_ld_1: pin names not known; wires that end beside it: in_2, not_1_out, reg4_inc_ld_1_p3, reg4_inc_ld_1_p4, reg4_inc_ld_1_p5, reg4_inc_ld_1_p6
  // DC4_16 dc4_16_1: pin names not known; wires that end beside it: rom16x20_1_dout[15:12], 1'b1, bruncnd, notPSWSTandFETCH, brnotFCBUS, brgrinst, brbezadr2, brjmp2, bradr2, brjmp4
  not not_2 (reg4_inc_ld_1_p6, reg4_inc_ld_1_p5);
  or or_3 (reg4_inc_ld_1_p5, bruncnd, brcnd);
  ROM16x20 rom16x20_1 (
    .A3__0(reg4_inc_ld_1_p4), .CS(1'b1),
    .DOUT({reg4_inc_ld_1_p3, rom16x20_1_dout, stEXEC, stADDR, clFETCH, ldIR15__0, ldIR31__16, ldMDR, rdMEM_t, incPC, ldMAR, MPGPR0, MPGPR1}));
  or or_4 (jmp4, INSTRUCBUS[7], INSTRUCBUS[8], INSTRUCBUS[9], INSTRUCBUS[10], INSTRUCBUS[11]);
  or or_5 (or_5_out, ADDRBUS[0], ADDRBUS[1]);
  or or_6 (or_6_out, ADDRBUS[2], ADDRBUS[3], ADDRBUS[4], ADDRBUS[5]);
  and and_1 (adr4, adr, or_5_out);
  and and_2 (adr2, adr, or_6_out);
  not not_3 (not_3_out, PSW[0]);
  not not_4 (not_4_out, PHASEFFBUS[0]);
  not not_5 (not_5_out, in_3);
  or or_7 (or_7_out, not_3_out, not_4_out);
  and and_3 (and_3_out, or_7_out, notPSWSTandFETCH);
  and and_4 (and_4_out, brnotFCBUS, not_5_out);
  and and_5 (and_5_out, brgrinst, in_4);
  and and_6 (and_6_out, brbezadr2, bezadr2);
  and and_7 (and_7_out, brjmp2, INSTRUCBUS[6]);
  and and_8 (and_8_out, brjmp4, jmp4);
  and and_9 (and_9_out, adr2, bradr2);
  or or_8 (brcnd, and_3_out, and_4_out, and_5_out, and_6_out, and_7_out, and_8_out, and_9_out);
  assign CMEMBUS[0] = ldMAR ? 1'b1 : 1'bz;  // Controlled_Buffer controlled_buffer_1
  assign CMEMBUS[2] = ldMDR ? 1'b1 : 1'bz;  // Controlled_Buffer controlled_buffer_2
  assign CMEMBUS[7] = incPC ? 1'b1 : 1'bz;  // Controlled_Buffer controlled_buffer_3
  assign CFFBUS[1] = clFETCH ? 1'b1 : 1'bz;  // Controlled_Buffer controlled_buffer_4
  assign CFFBUS[2] = stADDR ? 1'b1 : 1'bz;  // Controlled_Buffer controlled_buffer_5
  assign CFFBUS[4] = stEXEC ? 1'b1 : 1'bz;  // Controlled_Buffer controlled_buffer_6
  assign CREGBUS[0] = ldIR31__16 ? 1'b1 : 1'bz;  // Controlled_Buffer controlled_buffer_7
  assign CREGBUS[1] = ldIR15__0 ? 1'b1 : 1'bz;  // Controlled_Buffer controlled_buffer_8
  assign CREGBUS[8] = MPGPR1 ? 1'b1 : 1'bz;  // Controlled_Buffer controlled_buffer_9
  assign CREGBUS[9] = MPGPR0 ? 1'b1 : 1'bz;  // Controlled_Buffer controlled_buffer_10
  assign rdMEM = rdMEM_t ? 1'b1 : 1'bz;  // Controlled_Buffer controlled_buffer_11

  // Other names for the same wires on the sheet: immed = ADDRBUS[0]; memdir = ADDRBUS[1]; regdir = ADDRBUS[2];
  //   preincr = ADDRBUS[3]; postdec = ADDRBUS[4]; regindpom = ADDRBUS[5]; CLK = in_2; FCBUS = in_3; grinst = in_4;
  //   HALT = INSTRUCBUS[0]; RTS = INSTRUCBUS[1]; RTI = INSTRUCBUS[2]; INC = INSTRUCBUS[3]; PUSHGPR = INSTRUCBUS[4];
  //   POPGPR = INSTRUCBUS[5]; BLEQ = INSTRUCBUS[6]; jmp2 = INSTRUCBUS[6]; JEQ = INSTRUCBUS[7]; JGRTU = INSTRUCBUS[8];
  //   JGRT = INSTRUCBUS[9]; JMP = INSTRUCBUS[10]; JSR = INSTRUCBUS[11]; LD = INSTRUCBUS[12]; ST = INSTRUCBUS[13];
  //   ADD = INSTRUCBUS[14]; SUB = INSTRUCBUS[15]; CMP = INSTRUCBUS[16]; JADR = INSTRUCBUS[17]; CLR = INSTRUCBUS[18];
  //   FETCH = PHASEFFBUS[0]; ADDR = PHASEFFBUS[1]; EXEC = PHASEFFBUS[2]; INTR = PHASEFFBUS[3]; PSWSTART = PSW[0];
  //   rst = in_1

  // Notes on the sheet:
  //   Operaciona jedinica
  //   Kontrolna jedinica
endmodule

module ADDR (
  input  in_1,
  input  in_2,
  input  in_3,
  input  [3:0] PHASEFFBUS,
  input  [19:0] INSTRUCBUS,
  input  [5:0] ADDRBUS,
  output [19:0] CMEMBUS,
  output [7:0] CFFBUS,
  output rdMEM,
  output [18:0] CREGBUS
);

  wire and_1_out, and_2_out, and_3_out, bradr, brcnd, brnotADDR, brnotfcbus, brSTorJADR, bruncnd, clADDR,
       decB, incB, ldB, ldMAR, ldMDR, mxB0, mxB1, mxMAR0, mxMAR1, mxMAR2, not_1_out, not_3_out, not_4_out,
       rdMEM_t, reg5_cl_inc_ld_1_p5, reg5_cl_inc_ld_1_p6, stEXEC, STorJADR, wrGPR;
  wire [4:0] kmadr_1_a4__0, mp2_5b_1_y, reg5_cl_inc_ld_1_p4;
  wire [23:14] rom32x24_1_out;

  or or_1 (STorJADR, INSTRUCBUS[17], INSTRUCBUS[13]);
  // DC3_8 dc3_8_1: pin names not known; wires that end beside it: rom32x24_1_out[18:16], 1'b1, bruncnd, brnotADDR, brnotfcbus, brSTorJADR, bradr
  MP2_5b mp2_5b_1 (.En(1'b1), ._4__0(rom32x24_1_out[23:19]), .in_3(kmadr_1_a4__0), .S0(bradr), .Y(mp2_5b_1_y));
  not not_1 (not_1_out, in_1);
  // REG5_CL_INC_LD reg5_cl_inc_ld_1: pin names not known; wires that end beside it: in_2, not_1_out, mp2_5b_1_y, reg5_cl_inc_ld_1_p4, reg5_cl_inc_ld_1_p5, reg5_cl_inc_ld_1_p6
  KMADR kmadr_1 (
    .immed(ADDRBUS[0]), .memdir(ADDRBUS[1]), .regdir(ADDRBUS[2]), .preincr(ADDRBUS[3]), .postdec(ADDRBUS[4]),
    .regindpom(ADDRBUS[5]), .A4__0(kmadr_1_a4__0));
  not not_2 (reg5_cl_inc_ld_1_p6, reg5_cl_inc_ld_1_p5);
  ROM32x24 rom32x24_1 (
    .A7__0(reg5_cl_inc_ld_1_p4), .CS(1'b1),
    .OUT({rom32x24_1_out, mxMAR2, stEXEC, clADDR, ldMDR, rdMEM_t, decB, wrGPR, mxMAR1, incB, mxB1, mxMAR0, ldMAR, mxB0, ldB}));
  Pull_Resistor pull_resistor_1 (.node({rom32x24_1_out, mxMAR2, stEXEC, clADDR, ldMDR, rdMEM_t, decB, wrGPR, mxMAR1, incB, mxB1, mxMAR0, ldMAR, mxB0, ldB}));
  or or_2 (reg5_cl_inc_ld_1_p5, bruncnd, brcnd, bradr);
  not not_3 (not_3_out, PHASEFFBUS[1]);
  not not_4 (not_4_out, in_3);
  and and_1 (and_1_out, not_3_out, brnotADDR);
  and and_2 (and_2_out, not_4_out, brnotfcbus);
  and and_3 (and_3_out, brSTorJADR, STorJADR);
  or or_3 (brcnd, and_1_out, and_2_out, and_3_out);
  assign CMEMBUS[0] = ldMAR ? 1'b1 : 1'bz;  // Controlled_Buffer controlled_buffer_1
  assign CMEMBUS[2] = ldMDR ? 1'b1 : 1'bz;  // Controlled_Buffer controlled_buffer_2
  assign CMEMBUS[3] = mxMAR2 ? 1'b1 : 1'bz;  // Controlled_Buffer controlled_buffer_3
  assign CMEMBUS[4] = mxMAR1 ? 1'b1 : 1'bz;  // Controlled_Buffer controlled_buffer_4
  assign CMEMBUS[5] = mxMAR0 ? 1'b1 : 1'bz;  // Controlled_Buffer controlled_buffer_5
  assign CFFBUS[3] = clADDR ? 1'b1 : 1'bz;  // Controlled_Buffer controlled_buffer_6
  assign CFFBUS[4] = stEXEC ? 1'b1 : 1'bz;  // Controlled_Buffer controlled_buffer_7
  assign CREGBUS[7] = wrGPR ? 1'b1 : 1'bz;  // Controlled_Buffer controlled_buffer_8
  assign CREGBUS[10] = ldB ? 1'b1 : 1'bz;  // Controlled_Buffer controlled_buffer_9
  assign CREGBUS[11] = incB ? 1'b1 : 1'bz;  // Controlled_Buffer controlled_buffer_10
  assign CREGBUS[12] = decB ? 1'b1 : 1'bz;  // Controlled_Buffer controlled_buffer_11
  assign CREGBUS[14] = mxB1 ? 1'b1 : 1'bz;  // Controlled_Buffer controlled_buffer_12
  assign CREGBUS[15] = mxB0 ? 1'b1 : 1'bz;  // Controlled_Buffer controlled_buffer_13
  assign rdMEM = rdMEM_t ? 1'b1 : 1'bz;  // Controlled_Buffer controlled_buffer_14

  // Other names for the same wires on the sheet: immed = ADDRBUS[0]; memdir = ADDRBUS[1]; regdir = ADDRBUS[2];
  //   preincr = ADDRBUS[3]; postdec = ADDRBUS[4]; regindpom = ADDRBUS[5]; CLK = in_2; FCBUS = in_3;
  //   HALT = INSTRUCBUS[0]; RTS = INSTRUCBUS[1]; RTI = INSTRUCBUS[2]; INC = INSTRUCBUS[3]; PUSHGPR = INSTRUCBUS[4];
  //   POPGPR = INSTRUCBUS[5]; BLEQ = INSTRUCBUS[6]; JEQ = INSTRUCBUS[7]; JGRTU = INSTRUCBUS[8]; JGRT = INSTRUCBUS[9];
  //   JMP = INSTRUCBUS[10]; JSR = INSTRUCBUS[11]; LD = INSTRUCBUS[12]; ST = INSTRUCBUS[13]; ADD = INSTRUCBUS[14];
  //   SUB = INSTRUCBUS[15]; CMP = INSTRUCBUS[16]; JADR = INSTRUCBUS[17]; CLR = INSTRUCBUS[18]; FETCH = PHASEFFBUS[0];
  //   ADDR = PHASEFFBUS[1]; EXEC = PHASEFFBUS[2]; INTR = PHASEFFBUS[3]; rst = in_1

  // Notes on the sheet:
  //   Operaciona jedinica
  //   Upravljacka jedinica
endmodule

module EXEC (
  input  in_1,
  input  in_2,
  input  in_3,
  input  in_4,
  input  in_5,
  input  [15:0] B,
  input  [15:0] GPR,
  input  [3:0] PHASEFFBUS,
  input  [19:0] INSTRUCBUS,
  input  [5:0] ADDRBUS,
  input  [15:0] PSW,
  output out_12,
  output [15:0] ALU,
  output [19:0] CMEMBUS,
  output [7:0] CFFBUS,
  output [18:0] CREGBUS,
  output [6:0] CPSW,
  output rdMEM,
  output wrMEM
);

  wire add_t, and_1_out, and_2_out, and_3_out, and_4_out, brorjmp, or_1_out, or_2_out, sub_t, xor_1_out;

  xor xor_1 (xor_1_out, PSW[4], PSW[1]);
  or or_1 (or_1_out, xor_1_out, PSW[3]);
  or or_2 (or_2_out, PSW[3], PSW[2]);
  and and_1 (and_1_out, INSTRUCBUS[6], or_1_out);
  and and_2 (and_2_out, ~or_1_out, INSTRUCBUS[9]);  // AND_Gate
  and and_3 (and_3_out, PSW[3], INSTRUCBUS[7]);
  and and_4 (and_4_out, ~or_2_out, INSTRUCBUS[8]);  // AND_Gate
  or or_3 (brorjmp, and_1_out, and_2_out, and_3_out, and_4_out);
  ALU16_ADD_SUB alu16_add_sub_1 (
    .A15__0(GPR), .B15__0(B), .Cout(out_12), .Cin(1'b0), .add(add_t), .sub(sub_t), .ALU15__0(ALU));

  // Other names for the same wires on the sheet: immed = ADDRBUS[0]; memdir = ADDRBUS[1]; regdir = ADDRBUS[2];
  //   preincr = ADDRBUS[3]; postdec = ADDRBUS[4]; regindpom = ADDRBUS[5]; ALU15__0[15:0] = ALU; B15__0[15:0] = B;
  //   C16 = out_12; CLK = in_4; FCBUS = in_5; GPR15__0[15:0] = GPR; HALT = INSTRUCBUS[0]; RTS = INSTRUCBUS[1];
  //   RTI = INSTRUCBUS[2]; INC = INSTRUCBUS[3]; PUSHGPR = INSTRUCBUS[4]; POPGPR = INSTRUCBUS[5]; BLEQ = INSTRUCBUS[6];
  //   JEQ = INSTRUCBUS[7]; JGRTU = INSTRUCBUS[8]; JGRT = INSTRUCBUS[9]; JMP = INSTRUCBUS[10]; JSR = INSTRUCBUS[11];
  //   LD = INSTRUCBUS[12]; ST = INSTRUCBUS[13]; ADD = INSTRUCBUS[14]; SUB = INSTRUCBUS[15]; CMP = INSTRUCBUS[16];
  //   JADR = INSTRUCBUS[17]; CLR = INSTRUCBUS[18]; FETCH = PHASEFFBUS[0]; ADDR = PHASEFFBUS[1]; EXEC = PHASEFFBUS[2];
  //   INTR = PHASEFFBUS[3]; PSWV = PSW[1]; PSWC = PSW[2]; PSWZ = PSW[3]; PSWN = PSW[4]; PSWI = PSW[15]; rst = in_3;
  //   SC32 = in_2; SCN = in_1

  // Notes on the sheet:
  //   Operaciona jedinica
  //   Upravljacka jedinica
endmodule

module INTR (
  input  in_1,
  input  in_2,
  input  in_3,
  input  [3:0] PHASEFFBUS,
  input  [19:0] INSTRUCBUS,
  input  [15:0] PSW,
  input  [7:0] intr,
  output [15:0] ADDIVTP,
  output [2:0] UEXT2__0,
  output inta,
  output [19:0] CMEMBUS,
  output [7:0] CFFBUS,
  output [18:0] CREGBUS,
  output rdMEM,
  output wrMEM
);

  wire and_2_out, and_3_out, and_4_out, brcnd, brnotfcbus, brnotINTR, brnotprekid, bruncnd, clINTR, decSP,
       ldMAR, ldMDR, ldPC, MPGPR0, MPGPR1, mxGPR1, mxMAR0, mxMAR2, mxMDR0, mxMDR1, not_1_out, not_2_out,
       not_4_out, not_5_out, not_6_out, not_7_out, or_2_out, prekid, rdMEM_t, reg4_inc_ld_1_p5,
       reg4_inc_ld_1_p6, stFETCH, wrMEM_t;
  wire [2:0] IVTDSP15__0;
  wire [3:0] dc4_16_1_p1, reg4_inc_ld_1_p3, reg4_inc_ld_1_p4;
  wire [15:0] IVTP15__0;

  not not_1 (not_1_out, in_1);
  // REG16_LD reg16_ld_1: pin names not known; wires that end beside it: in_2, not_1_out, IVTP15__0
  not not_2 (not_2_out, in_1);
  // DC4_16 dc4_16_1: pin names not known; wires that end beside it: dc4_16_1_p1, 1'b1, bruncnd, brnotINTR, brnotprekid, brnotfcbus
  // REG4_INC_LD reg4_inc_ld_1: pin names not known; wires that end beside it: in_2, not_2_out, reg4_inc_ld_1_p3, reg4_inc_ld_1_p4, reg4_inc_ld_1_p5, reg4_inc_ld_1_p6
  and and_1 (prekid, or_2_out, PSW[15], not_4_out);
  not not_3 (reg4_inc_ld_1_p6, reg4_inc_ld_1_p5);
  ROM16x24 rom16x24_1 (
    .A3__0(reg4_inc_ld_1_p4), .CS(1'b1),
    .DOUT({reg4_inc_ld_1_p3, dc4_16_1_p1, clINTR, stFETCH, ldPC, mxGPR1, rdMEM_t, mxMAR0, inta, mxMDR1, MPGPR0, wrMEM_t, mxMDR0, MPGPR1, ldMDR, ldMAR, decSP, mxMAR2}));
  not not_4 (not_4_out, INSTRUCBUS[0]);
  or or_1 (reg4_inc_ld_1_p5, bruncnd, brcnd);
  or or_2 (or_2_out, intr[7], intr[6], intr[5], intr[4], intr[3], intr[2], intr[1], intr[0]);
  // CD8 cd8_1: pin names not known; wires that end beside it: intr[7], intr[6], intr[5], intr[4], intr[3], intr[2], intr[1], intr[0], 1'b1, UEXT2__0[2], UEXT2__0[1], UEXT2__0[0]
  // REG3_LD reg3_ld_1: pin names not known; wires that end beside it: in_2, UEXT2__0, IVTDSP15__0, inta
  not not_5 (not_5_out, PHASEFFBUS[3]);
  and and_2 (and_2_out, not_5_out, brnotINTR);
  not not_6 (not_6_out, prekid);
  and and_3 (and_3_out, not_6_out, brnotprekid);
  not not_7 (not_7_out, in_3);
  and and_4 (and_4_out, not_7_out, brnotfcbus);
  or or_3 (brcnd, and_2_out, and_3_out, and_4_out);
  // ADD16 add16_1: pin names not known; wires that end beside it: IVTP15__0, ADDIVTP, {{13{1'b0}}, IVTDSP15__0}, 1'b0
  assign CMEMBUS[0] = ldMAR ? 1'b1 : 1'bz;  // Controlled_Buffer controlled_buffer_1
  assign CMEMBUS[2] = ldMDR ? 1'b1 : 1'bz;  // Controlled_Buffer controlled_buffer_2
  assign CMEMBUS[3] = mxMAR2 ? 1'b1 : 1'bz;  // Controlled_Buffer controlled_buffer_3
  assign CMEMBUS[5] = mxMAR0 ? 1'b1 : 1'bz;  // Controlled_Buffer controlled_buffer_4
  assign CMEMBUS[6] = mxMDR0 ? 1'b1 : 1'bz;  // Controlled_Buffer controlled_buffer_5
  assign CMEMBUS[8] = ldPC ? 1'b1 : 1'bz;  // Controlled_Buffer controlled_buffer_6
  assign CMEMBUS[10] = decSP ? 1'b1 : 1'bz;  // Controlled_Buffer controlled_buffer_7
  assign CMEMBUS[11] = mxMDR1 ? 1'b1 : 1'bz;  // Controlled_Buffer controlled_buffer_8
  assign CFFBUS[0] = stFETCH ? 1'b1 : 1'bz;  // Controlled_Buffer controlled_buffer_9
  assign CFFBUS[7] = clINTR ? 1'b1 : 1'bz;  // Controlled_Buffer controlled_buffer_10
  assign CREGBUS[5] = mxGPR1 ? 1'b1 : 1'bz;  // Controlled_Buffer controlled_buffer_11
  assign CREGBUS[8] = MPGPR1 ? 1'b1 : 1'bz;  // Controlled_Buffer controlled_buffer_12
  assign CREGBUS[9] = MPGPR0 ? 1'b1 : 1'bz;  // Controlled_Buffer controlled_buffer_13
  assign rdMEM = rdMEM_t ? 1'b1 : 1'bz;  // Controlled_Buffer controlled_buffer_14
  assign wrMEM = wrMEM_t ? 1'b1 : 1'bz;  // Controlled_Buffer controlled_buffer_15

  // Other names for the same wires on the sheet: ldBR = inta; ADDIVTP15__0[15:0] = ADDIVTP; CLK = in_2; FCBUS = in_3;
  //   HALT = INSTRUCBUS[0]; RTS = INSTRUCBUS[1]; RTI = INSTRUCBUS[2]; INC = INSTRUCBUS[3]; PUSHGPR = INSTRUCBUS[4];
  //   POPGPR = INSTRUCBUS[5]; BLEQ = INSTRUCBUS[6]; JEQ = INSTRUCBUS[7]; JGRTU = INSTRUCBUS[8]; JGRT = INSTRUCBUS[9];
  //   JMP = INSTRUCBUS[10]; JSR = INSTRUCBUS[11]; LD = INSTRUCBUS[12]; ST = INSTRUCBUS[13]; ADD = INSTRUCBUS[14];
  //   SUB = INSTRUCBUS[15]; CMP = INSTRUCBUS[16]; JADR = INSTRUCBUS[17]; CLR = INSTRUCBUS[18]; intr7__0[7:0] = intr;
  //   FETCH = PHASEFFBUS[0]; ADDR = PHASEFFBUS[1]; EXEC = PHASEFFBUS[2]; INTR_t = PHASEFFBUS[3]; PSWI = PSW[15];
  //   rst = in_1

  // Notes on the sheet:
  //   Operaciona jedinica
  //   Upravljacka jedinica
endmodule

module RAM (
  input  [15:0] in_1,
  input  in_2,
  input  [15:0] in_3,
  input  in_4,
  input  in_5,
  input  in_6,
  output [15:0] out_7,
  output out_8
);

  wire and_1_out, and_2_out, CNT0, LDCNT, not_1_out, notCNT0, or_1_out, reg4_ld_sl_sr_1_p6, rsff_2_p4,
       rsff_2_p5, rsff_3_p4, sl;
  wire [3:0] CNT, LFSR;

  // RSFF rsff_1: pin names not known; wires that end beside it: 1'b0, in_2, in_6, sl
  or or_1 (or_1_out, in_4, in_5);
  // REG4_LD_SL_SR reg4_ld_sl_sr_1: pin names not known; wires that end beside it: 1'b0, 1'b0, in_2, 4'b1111, LFSR, reg4_ld_sl_sr_1_p6, sl, in_6
  // RisingEdge risingedge_1: pin names not known; wires that end beside it: or_1_out, in_2, LDCNT
  MEM64Kx16 mem64kx16_1 (.WR_RD(in_4), .A15__0(in_1), .DIN(in_3), .CS(1'b1), .CLK(in_2), .DOUT(out_7));
  xor xor_1 (reg4_ld_sl_sr_1_p6, LFSR[2], LFSR[3]);
  and and_1 (and_1_out, CNT0, not_1_out);
  not not_1 (not_1_out, LDCNT);
  // RSFF rsff_2: pin names not known; wires that end beside it: and_1_out, in_2, LDCNT, rsff_2_p4, rsff_2_p5
  not not_2 (rsff_2_p4, in_6);
  and and_2 (and_2_out, rsff_2_p5, CNT0);
  // REG4m_DEC_LD reg4m_dec_ld_1: pin names not known; wires that end beside it: in_2, LFSR, CNT, LDCNT, notCNT0, notCNT0
  or or_2 (notCNT0, CNT[0], CNT[1], CNT[2], CNT[3]);
  // RSFF rsff_3: pin names not known; wires that end beside it: out_8, in_2, and_2_out, rsff_3_p4, out_8
  not not_3 (rsff_3_p4, in_6);
  not not_4 (CNT0, notCNT0);

  // Other names for the same wires on the sheet: ADR[15:0] = in_1; CLK = in_2; DIN[15:0] = in_3; DOUT[15:0] = out_7;
  //   fc = out_8; RDMEM = in_5; rst = in_6; WRMEM = in_4

  // Notes on the sheet:
  //   Random broj predstavlja vreme pristupa memoriji
  //   Brojac za generisanje random broja 
  //   Jedinica za generisanje function complete (fc) signala
  //   Brojac za dekrementiranje random broja
endmodule
